// Logisim project lab01.circ as structural Verilog: 1 circuit, main circuit main
module main (
  input  A,
  input  A_2,
  input  B,
  input  A_3,
  input  B_2,
  input  A_4,
  input  p,
  input  A_5,
  input  B_3,
  output Not_A,
  output A_and_B,
  output A_or_not_B,
  output A_or_B,
  output A_and_not_B
);

  wire transistor_3_out, transistor_8_out, transistor_11_out, transistor_17_out;

  Transistor transistor_1 (.in(1'b1), .out(Not_A), .gate(A));
  Transistor #(.\type ("n")) transistor_2 (.in(1'b0), .out(Not_A), .gate(A));
  Transistor #(.\type ("n")) transistor_3 (.in(1'b1), .out(transistor_3_out), .gate(A_2));
  Transistor #(.\type ("n")) transistor_4 (.in(transistor_3_out), .out(A_and_B), .gate(B));
  Transistor transistor_5 (.in(1'b0), .out(A_and_B), .gate(A_2));
  Transistor #(.\type ("n")) transistor_6 (.in(1'b1), .out(A_or_B), .gate(A_4));
  Transistor #(.\type ("n")) transistor_7 (.in(1'b1), .out(A_or_B), .gate(p));
  Transistor transistor_8 (.in(1'b0), .out(transistor_8_out), .gate(A_4));
  Transistor transistor_9 (.in(1'b0), .out(A_and_B), .gate(B));
  Transistor transistor_10 (.in(transistor_8_out), .out(A_or_B), .gate(p));
  Transistor transistor_11 (.in(1'b1), .out(transistor_11_out), .gate(A_3));
  Transistor transistor_12 (.in(1'b1), .out(A_and_not_B), .gate(A_5));
  Transistor transistor_13 (.in(transistor_11_out), .out(A_or_not_B), .gate(B_2));
  Transistor #(.\type ("n")) transistor_14 (.in(1'b0), .out(A_or_not_B), .gate(A_3));
  Transistor #(.\type ("n")) transistor_15 (.in(1'b0), .out(A_or_not_B), .gate(B_2));
  Transistor transistor_16 (.in(1'b1), .out(A_and_not_B), .gate(B_3));
  Transistor #(.\type ("n")) transistor_17 (.in(1'b0), .out(transistor_17_out), .gate(A_5));
  Transistor #(.\type ("n")) transistor_18 (.in(transistor_17_out), .out(A_and_not_B), .gate(B_3));

  // Notes on the sheet:
  //   p
  //   n
  //   n
  //   p
  //   n
  //   p
  //   p
  //   p
  //   n
  //   p
  //   n
  //   p
  //   n
  //   p
  //   n
endmodule
